# Fritzing sketch Arduino Anschlussplan updated (saved by Fritzing 0.9.3b)
breadboards: 2

parts:
  Bauteil1 = Arduino Nano (Rev3.0) (ICSP)
  Bauteil2 = BME280 Breakout
  SW1 = DIP Switch 8 Position [package=dipswitch-08]
  J1 = Piezo Speaker
  Q1 = LTR-301 [package=ltr-301]
  LED1 = RGB LED (com. cathode, rbg) [package="5 mm [THT]"]
  S1 = Pushbutton [package="[THT]"]
  Chirp!_Soil_Moisture_Sensor2 = Chirp! Soil Moisture Sensor v2.7.3
  R1 = Resistor [tolerance=±5% resistance=10k package="2010 [SMD]"]
  R2 = Resistor [tolerance=±5% resistance=10k package="2010 [SMD]"]
  R3 = Resistor [tolerance=±5% resistance=10k package="2010 [SMD]"]
  R4 = Resistor [tolerance=±5% resistance=10k package="2010 [SMD]"]
  R5 = Resistor [tolerance=±5% resistance=10k package="2010 [SMD]"]
  USBTTL2 = Micro USB B Plug  # not connected
  VCC2 = Battery  # not connected
  X1 = USB Connectors [package=usb-a-s-nosilk-female]  # not connected
  USBTTL3 = USB A Plug  # not connected

nets:
  GND: Bauteil1.GND, Bauteil2.GND, LED1.common_cathode, Chirp!_Soil_Moisture_Sensor2.pin_5
  N1: Bauteil1.D4, SW1.16
  N2: Bauteil1.D5, SW1.15
  N3: Bauteil1.D6, SW1.14
  N4: Bauteil1.D7, SW1.13
  N5: Bauteil1.D8, SW1.12
  N6: Bauteil1.D9, SW1.11
  N7: Bauteil1.D10, SW1.10
  N8: Bauteil1.D11/MOSI, SW1.9
  N9: Bauteil1.D12/MISO, S1.Pin_3, S1.Pin_4, R1.Pin_0
  N10: Bauteil1.A7, J1.pin2
  N11: Bauteil1.A6, Chirp!_Soil_Moisture_Sensor2.pin_3
  N12: Bauteil1.A5, Bauteil2.SCK/SCL
  N13: Bauteil1.A4, Bauteil2.SDI/SDA
  N14: Bauteil1.A3, R2.Pin_0
  N15: Bauteil1.A2, R4.Pin_0
  N16: Bauteil1.A1, R3.Pin_0
  N17: Bauteil1.A0, Q1.E, R5.Pin_0
  3V3: Bauteil1.3V3, Bauteil2.3.3V, SW1.1, SW1.2, SW1.3, SW1.4, SW1.5, SW1.6, SW1.7, SW1.8, S1.Pin_1, S1.Pin_2, Chirp!_Soil_Moisture_Sensor2.Pin_1
  N18: J1.pin1, R5.Pin_1
  N19: LED1.red_anode, R2.Pin_1
  N20: LED1.blue_anode, R4.Pin_1
  N21: LED1.green_anode, R3.Pin_1

notes:
  Da es keine Powerbank in Fritzing gibt, hab ich selber eine "erstellt". Es sollte eine Powerbank mit einem USB - A zu USB - Micro darstellen.
  Wird beim Arduino eingesteckt.
