# Fritzing sketch Arduino_Anschlussplan_aktuell (saved by Fritzing 0.9.6b)
breadboards: 2

parts:
  Bauteil1 = Arduino Nano (Rev3.0) (ICSP)
  SW1 = DIP Switch 8 Position [package=dipswitch-08]
  J1 = Piezo Speaker
  LED1 = RGB LED (com. cathode, rbg) [package="5 mm [THT]"]
  R1 = Resistor [tolerance=±5% resistance=10k package="2010 [SMD]"]
  Chirp!_Soil_Moisture_Sensor3 = Chirp! Soil Moisture Sensor v2.7.3
  Bauteil3 = BME280 Breakout
  R6 = Resistor [tolerance=±5% resistance=2k package="2010 [SMD]"]
  R7 = Resistor [tolerance=±5% resistance=220 package="2010 [SMD]"]
  R8 = Resistor [tolerance=±5% resistance=220 package="2010 [SMD]"]
  R9 = Resistor [tolerance=±5% resistance=220 package="2010 [SMD]"]
  S2 = Pushbutton [package="[THT]"]
  Q3 = LTR-301 [package=ltr-301]
  R10 = Resistor [tolerance=±5% resistance=10k package="2010 [SMD]"]
  R11 = Resistor [tolerance=±5% resistance=10k package="2010 [SMD]"]
  R12 = Resistor [tolerance=±5% resistance=10k package="2010 [SMD]"]
  R13 = Resistor [tolerance=±5% resistance=10k package="2010 [SMD]"]
  R14 = Resistor [tolerance=±5% resistance=10k package="2010 [SMD]"]
  R15 = Resistor [tolerance=±5% resistance=10k package="2010 [SMD]"]
  R16 = Resistor [tolerance=±5% resistance=10k package="2010 [SMD]"]
  R17 = Resistor [tolerance=±5% resistance=10k package="2010 [SMD]"]

nets:
  GND: Bauteil1.GND, J1.pin1, LED1.common_cathode, R1.Pin_1, Chirp!_Soil_Moisture_Sensor3.pin_5, Bauteil3.GND, R6.Pin_1, R10.Pin_1, R11.Pin_1, R12.Pin_1, R13.Pin_1, R14.Pin_1, R15.Pin_1, R16.Pin_1, R17.Pin_1
  N1: Bauteil1.D4, SW1.16, R10.Pin_0
  N2: Bauteil1.D5, SW1.15, R11.Pin_0
  N3: Bauteil1.D6, SW1.14, R12.Pin_0
  N4: Bauteil1.D7, SW1.13, R13.Pin_0
  N5: Bauteil1.D8, SW1.12, R14.Pin_0
  N6: Bauteil1.D9, SW1.11, R15.Pin_0
  N7: Bauteil1.D10, SW1.10, R16.Pin_0
  N8: Bauteil1.D11/MOSI, SW1.9, R17.Pin_0
  N9: Bauteil1.D12/MISO, R1.Pin_0, S2.Pin_3, S2.Pin_4
  N10: Bauteil1.A7, J1.pin2
  N11: Bauteil1.A6, Chirp!_Soil_Moisture_Sensor3.pin_3
  N12: Bauteil1.A5, Bauteil3.SCK/SCL
  N13: Bauteil1.A4, Bauteil3.SDI/SDA
  N14: Bauteil1.A3, R8.Pin_1
  N15: Bauteil1.A2, R7.Pin_1
  N16: Bauteil1.A1, R9.Pin_1
  N17: Bauteil1.A0, R6.Pin_0, Q3.E
  3V3: Bauteil1.3V3, SW1.1, SW1.2, SW1.3, SW1.4, SW1.5, SW1.6, SW1.7, SW1.8, Chirp!_Soil_Moisture_Sensor3.Pin_1, Bauteil3.3.3V, S2.Pin_1, S2.Pin_2, Q3.C
  N18: LED1.red_anode, R8.Pin_0
  N19: LED1.blue_anode, R7.Pin_0
  N20: LED1.green_anode, R9.Pin_0

notes:
  Da es keine Powerbank in Fritzing gibt, hab ich selber eine "erstellt". Es sollte eine Powerbank mit einem USB - A zu USB - Micro darstellen.
  Wird beim Arduino eingesteckt.
